# Fritzing sketch midi_light_show_extended (saved by Fritzing 0.9.3b)
breadboards: 1

parts:
  Raspberry_Pi_1 = Raspberry Pi 3 [part_number=RPI-3-V1.2]
  LED2 = LED - 5mm [color="Red (633nm)" package="5 mm [THT]"]
  LED3 = LED - 5mm [color="Green (565nm)" package="5 mm [THT]"]
  LED4 = LED - 5mm [color="Blue (430nm)" package="5 mm [THT]"]
  LED5 = LED - 5mm [color="Yellow (595nm)" package="5 mm [THT]"]
  LED6 = LED - 5mm [color="Red (633nm)" package="5 mm [THT]"]
  LED7 = LED - 5mm [color="Green (565nm)" package="5 mm [THT]"]
  LED8 = LED - 5mm [color="Blue (430nm)" package="5 mm [THT]"]
  LED9 = LED - 5mm [color="Yellow (595nm)" package="5 mm [THT]"]
  R5 = Resistor [tolerance=±5% resistance=220 package=THT]
  R6 = Resistor [tolerance=±5% resistance=220 package=THT]
  R7 = Resistor [tolerance=±5% resistance=220 package=THT]
  R8 = Resistor [tolerance=±5% resistance=220 package=THT]
  R9 = Resistor [tolerance=±5% resistance=220 package=THT]
  R10 = Resistor [tolerance=±5% resistance=220 package=THT]
  R11 = Resistor [tolerance=±5% resistance=220 package=THT]
  R12 = Resistor [tolerance=±5% resistance=220 package=THT]
  LED10 = LED - 5mm [color="Red (633nm)" package="5 mm [THT]"]
  LED11 = LED - 5mm [color="Green (565nm)" package="5 mm [THT]"]
  LED12 = LED - 5mm [color="Blue (430nm)" package="5 mm [THT]"]
  LED13 = LED - 5mm [color="Yellow (595nm)" package="5 mm [THT]"]
  LED14 = LED - 5mm [color="Red (633nm)" package="5 mm [THT]"]
  LED15 = LED - 5mm [color="Green (565nm)" package="5 mm [THT]"]
  LED16 = LED - 5mm [color="Blue (430nm)" package="5 mm [THT]"]
  LED17 = LED - 5mm [color="Yellow (595nm)" package="5 mm [THT]"]
  R13 = Resistor [tolerance=±5% resistance=220 package=THT]  # not connected
  R14 = Resistor [tolerance=±5% resistance=220 package=THT]
  R15 = Resistor [tolerance=±5% resistance=220 package=THT]
  R16 = Resistor [tolerance=±5% resistance=220 package=THT]
  R17 = Resistor [tolerance=±5% resistance=220 package=THT]
  R18 = Resistor [tolerance=±5% resistance=220 package=THT]
  R19 = Resistor [tolerance=±5% resistance=220 package=THT]
  R20 = Resistor [tolerance=±5% resistance=220 package=THT]
  LED18 = LED - 5mm [color="Red (633nm)" package="5 mm [THT]"]
  LED19 = LED - 5mm [color="Green (565nm)" package="5 mm [THT]"]
  R21 = Resistor [tolerance=±5% resistance=220 package=THT]

nets:
  N1: Raspberry_Pi_1.GIPO27, LED19.anode
  N2: Raspberry_Pi_1.GIPO22, LED18.anode
  N3: Raspberry_Pi_1.GIPO10, LED17.anode
  N4: Raspberry_Pi_1.GIPO9, LED16.anode
  N5: Raspberry_Pi_1.GIPO11, LED15.anode
  N6: Raspberry_Pi_1.GIPO5, LED4.anode
  N7: Raspberry_Pi_1.GIPO6, LED3.anode
  N8: Raspberry_Pi_1.GIPO13, LED2.anode
  N9: Raspberry_Pi_1.GIPO19, LED14.anode
  N10: Raspberry_Pi_1.GIPO26, LED11.anode
  N11: Raspberry_Pi_1.GND, R7.Pin_0, R8.Pin_0, R9.Pin_0, R11.Pin_0, R15.Pin_0, R17.Pin_0, R19.Pin_0, R20.Pin_0, R21.Pin_0
  N12: Raspberry_Pi_1.GIPO21, LED10.anode
  N13: Raspberry_Pi_1.GIPO20, LED12.anode
  N14: Raspberry_Pi_1.GIPO16, LED13.anode
  N15: Raspberry_Pi_1.GIPO7, LED5.anode
  N16: Raspberry_Pi_1.GIPO23, LED6.anode
  N17: Raspberry_Pi_1.GIPO18, LED7.anode
  N18: Raspberry_Pi_1.GIPO15, LED8.anode
  N19: Raspberry_Pi_1.GIPO14, LED9.anode
  N20: LED2.cathode, R8.Pin_1
  N21: LED3.cathode, R6.Pin_1
  N22: LED4.cathode, R7.Pin_1
  N23: LED5.cathode, R5.Pin_1
  N24: LED6.cathode, R9.Pin_1
  N25: LED7.cathode, R10.Pin_1
  N26: LED8.cathode, R11.Pin_1
  N27: LED9.cathode, R12.Pin_1
  N28: LED11.cathode, R14.Pin_1
  N29: LED12.cathode, R15.Pin_1
  N30: LED13.cathode, R16.Pin_1
  N31: LED14.cathode, R17.Pin_1
  N32: LED15.cathode, R18.Pin_1
  N33: LED16.cathode, R19.Pin_1
  N34: LED17.cathode, R20.Pin_1
  N35: LED18.cathode, R21.Pin_1

notes:
  Raspberry Pi 3 B+
  LEDs:
  RED, GPIO 13
  GREEN, GPIO 06
  BLUE, GPIO 05
  YELLOW, GPIO 07
  RED, GPIO 23
  GREEN, GPIO 18
  BLUE, GPIO 15
  YELLOW, GPIO 14
  RED, GPIO 21
  GREEN, GPIO 26
  BLUE, GPIO 20
  YELLOW, GPIO 16
  RED, GPIO 19
  GREEN, GPIO
  BLUE, GPIO
  YELLOW, GPIO
  RED, GPIO 22
  GREEN, GPIO 27
